// Digital circuit 8_Bit_adder_CMOS.dig as structural Verilog
module _8_Bit_adder_CMOS (
  input  B_0,
  input  B_1,
  input  B_2,
  input  B_3,
  input  B_4,
  input  B_5,
  input  B_6,
  input  B_7,
  input  A_0,
  input  A_1,
  input  A_2,
  input  A_3,
  input  A_4,
  input  A_5,
  input  A_6,
  input  A_7,
  output OUT_7,
  output OUT_6,
  output OUT_5,
  output OUT_0,
  output OUT_4,
  output OUT_3,
  output OUT_2,
  output OUT_1,
  output Carry_out
);

  wire A_0_NOT, A_1_B_1, A_1_B_1____Carry_0_A_1, A_1_B_1_NOT, A_1_NAND_B_1, A_1_NAND_Carry_0, A_1_NOT,
       A_2_B_2, A_2_B_2____Carry_1_A_2, A_2_B_2_NOT, A_2_NAND_B_2, A_2_NAND_Carry_1, A_2_NOT, A_3_B_3,
       A_3_B_3____Carry_2_A_3, A_3_B_3_NOT, A_3_NAND_B_3, A_3_NAND_Carry_2, A_3_NOT, A_4_B_4,
       A_4_B_4____Carry_3_A_4, A_4_B_4_NOT, A_4_NAND_B_4, A_4_NAND_Carry_3, A_4_NOT, A_5_B_5,
       A_5_B_5____Carry_4_A_5, A_5_B_5_NOT, A_5_NAND_B_5, A_5_NAND_Carry_4, A_5_NOT, A_6_B_6,
       A_6_B_6____Carry_5_A_6, A_6_B_6_NOT, A_6_NAND_B_6, A_6_NAND_Carry_5, A_6_NOT, A_7_B_7,
       A_7_B_7____Carry_6_A_7, A_7_B_7_NOT, A_7_NAND_B_7, A_7_NAND_Carry_6, A_7_NOT, B_0_NOT,
       B_1_NAND_Carry_0, B_1_NOT, B_2_NAND_Carry_1, B_2_NOT, B_3_NAND_Carry_2, B_3_NOT, B_4_NAND_Carry_3,
       B_4_NOT, B_5_NAND_Carry_4, B_5_NOT, B_6_NAND_Carry_5, B_6_NOT, B_7_NAND_Carry_6, B_7_NOT, C_0_NOT,
       C_1_NOT, C_2_NOT, C_3_NOT, C_4_NOT, C_5_NOT, C_6_NOT, Carry_0, Carry_1, Carry_2, Carry_3, Carry_4,
       Carry_5, Carry_6, GND, nfet_6_s, nfet_8_s, nfet_10_s, nfet_12_s, nfet_15_s, nfet_17_s, nfet_20_s,
       nfet_25_s, nfet_33_s, nfet_35_s, nfet_37_s, nfet_39_s, nfet_41_s, nfet_43_s, nfet_45_s, nfet_47_s,
       nfet_49_s, nfet_55_s, nfet_57_s, nfet_59_s, nfet_61_s, nfet_63_s, nfet_65_s, nfet_67_s, nfet_69_s,
       nfet_71_s, nfet_73_s, nfet_75_s, nfet_77_s, nfet_79_s, nfet_84_s, nfet_86_s, nfet_88_s, nfet_90_s,
       nfet_92_s, nfet_94_s, nfet_97_s, nfet_101_s, nfet_104_s, nfet_106_s, nfet_108_s, nfet_110_s,
       nfet_112_s, nfet_114_s, nfet_122_s, nfet_124_s, nfet_126_s, nfet_128_s, nfet_130_s, nfet_132_s,
       nfet_135_s, nfet_139_s, nfet_141_s, nfet_143_s, nfet_145_s, nfet_147_s, nfet_149_s, nfet_151_s,
       nfet_153_s, nfet_155_s, nfet_157_s, nfet_159_s, nfet_161_s, nfet_164_s, nfet_167_s, nfet_169_s,
       pfet_6_d, pfet_8_d, pfet_15_d, pfet_17_d, pfet_35_d, pfet_37_d, pfet_38_d, pfet_40_d, pfet_55_d,
       pfet_57_d, pfet_59_d, pfet_84_d, pfet_85_d, pfet_86_d, pfet_87_d, pfet_104_d, pfet_124_d, pfet_126_d,
       pfet_128_d, pfet_139_d, pfet_141_d, pfet_157_d, pfet_158_d, Pull_up_Resistor;

  PullDown pulldown_1 (.out(GND));
  PullUp pullup_1 (.out(Pull_up_Resistor));
  PFET pfet_1 (.G(A_1), .S(Pull_up_Resistor), .D(A_1_NOT));
  NFET nfet_1 (.G(A_1), .D(A_1_NOT), .S(GND));
  PFET pfet_2 (.G(B_1), .S(Pull_up_Resistor), .D(B_1_NOT));
  NFET nfet_2 (.G(B_1), .D(B_1_NOT), .S(GND));
  PFET pfet_3 (.G(Carry_0), .S(Pull_up_Resistor), .D(C_0_NOT));
  NFET nfet_3 (.G(Carry_0), .D(C_0_NOT), .S(GND));
  PFET pfet_4 (.G(A_0), .S(Pull_up_Resistor), .D(A_0_NOT));
  NFET nfet_4 (.G(A_0), .D(A_0_NOT), .S(GND));
  PFET pfet_5 (.G(B_0), .S(Pull_up_Resistor), .D(B_0_NOT));
  NFET nfet_5 (.G(B_0), .D(B_0_NOT), .S(GND));
  PFET pfet_6 (.G(A_1), .S(Pull_up_Resistor), .D(pfet_6_d));
  PFET pfet_7 (.G(A_1_NOT), .S(pfet_6_d), .D(A_1_B_1));
  NFET nfet_6 (.G(A_1), .D(A_1_B_1), .S(nfet_6_s));
  NFET nfet_7 (.G(B_1), .D(nfet_6_s), .S(GND));
  PFET pfet_8 (.G(A_0), .S(Pull_up_Resistor), .D(pfet_8_d));
  PFET pfet_9 (.G(A_0_NOT), .S(pfet_8_d), .D(OUT_0));
  NFET nfet_8 (.G(A_0), .D(OUT_0), .S(nfet_8_s));
  NFET nfet_9 (.G(B_0), .D(nfet_8_s), .S(GND));
  PFET pfet_10 (.G(B_0), .S(Pull_up_Resistor), .D(pfet_8_d));
  PFET pfet_11 (.G(B_0_NOT), .S(pfet_8_d), .D(OUT_0));
  NFET nfet_10 (.G(A_0_NOT), .D(OUT_0), .S(nfet_10_s));
  NFET nfet_11 (.G(B_0_NOT), .D(nfet_10_s), .S(GND));
  PFET pfet_12 (.G(B_1), .S(Pull_up_Resistor), .D(pfet_6_d));
  PFET pfet_13 (.G(B_1_NOT), .S(pfet_6_d), .D(A_1_B_1));
  NFET nfet_12 (.G(A_1_NOT), .D(A_1_B_1), .S(nfet_12_s));
  NFET nfet_13 (.G(B_1_NOT), .D(nfet_12_s), .S(GND));
  PFET pfet_14 (.G(A_1_B_1), .S(Pull_up_Resistor), .D(A_1_B_1_NOT));
  NFET nfet_14 (.G(A_1_B_1), .D(A_1_B_1_NOT), .S(GND));
  PFET pfet_15 (.G(A_0), .S(Pull_up_Resistor), .D(pfet_15_d));
  PFET pfet_16 (.G(B_0), .S(Pull_up_Resistor), .D(pfet_15_d));
  NFET nfet_15 (.G(A_0), .D(pfet_15_d), .S(nfet_15_s));
  NFET nfet_16 (.G(B_0), .D(nfet_15_s), .S(GND));
  PFET pfet_17 (.G(A_1_B_1), .S(Pull_up_Resistor), .D(pfet_17_d));
  PFET pfet_18 (.G(A_1_B_1_NOT), .S(pfet_17_d), .D(OUT_1));
  NFET nfet_17 (.G(A_1_B_1), .D(OUT_1), .S(nfet_17_s));
  NFET nfet_18 (.G(Carry_0), .D(nfet_17_s), .S(GND));
  PFET pfet_19 (.G(pfet_15_d), .S(Pull_up_Resistor), .D(Carry_0));
  NFET nfet_19 (.G(pfet_15_d), .D(Carry_0), .S(GND));
  PFET pfet_20 (.G(Carry_0), .S(Pull_up_Resistor), .D(pfet_17_d));
  PFET pfet_21 (.G(C_0_NOT), .S(pfet_17_d), .D(OUT_1));
  NFET nfet_20 (.G(A_1_B_1_NOT), .D(OUT_1), .S(nfet_20_s));
  NFET nfet_21 (.G(C_0_NOT), .D(nfet_20_s), .S(GND));
  PFET pfet_22 (.G(A_5), .S(Pull_up_Resistor), .D(A_5_NOT));
  NFET nfet_22 (.G(A_5), .D(A_5_NOT), .S(GND));
  PFET pfet_23 (.G(B_5), .S(Pull_up_Resistor), .D(B_5_NOT));
  NFET nfet_23 (.G(B_5), .D(B_5_NOT), .S(GND));
  PFET pfet_24 (.G(Carry_4), .S(Pull_up_Resistor), .D(C_4_NOT));
  NFET nfet_24 (.G(Carry_4), .D(C_4_NOT), .S(GND));
  PFET pfet_25 (.G(A_1), .S(Pull_up_Resistor), .D(A_1_NAND_B_1));
  NFET nfet_25 (.G(A_1), .D(A_1_NAND_B_1), .S(nfet_25_s));
  NFET nfet_26 (.G(B_1), .D(nfet_25_s), .S(GND));
  PFET pfet_26 (.G(A_1), .S(Pull_up_Resistor), .D(A_1_NAND_Carry_0));
  PFET pfet_27 (.G(A_3), .S(Pull_up_Resistor), .D(A_3_NOT));
  NFET nfet_27 (.G(A_3), .D(A_3_NOT), .S(GND));
  PFET pfet_28 (.G(B_3), .S(Pull_up_Resistor), .D(B_3_NOT));
  NFET nfet_28 (.G(B_3), .D(B_3_NOT), .S(GND));
  PFET pfet_29 (.G(Carry_2), .S(Pull_up_Resistor), .D(C_2_NOT));
  NFET nfet_29 (.G(Carry_2), .D(C_2_NOT), .S(GND));
  PFET pfet_30 (.G(A_7), .S(Pull_up_Resistor), .D(A_7_NOT));
  NFET nfet_30 (.G(A_7), .D(A_7_NOT), .S(GND));
  PFET pfet_31 (.G(B_7), .S(Pull_up_Resistor), .D(B_7_NOT));
  NFET nfet_31 (.G(B_7), .D(B_7_NOT), .S(GND));
  PFET pfet_32 (.G(Carry_6), .S(Pull_up_Resistor), .D(C_6_NOT));
  NFET nfet_32 (.G(Carry_6), .D(C_6_NOT), .S(GND));
  PFET pfet_33 (.G(B_1), .S(Pull_up_Resistor), .D(A_1_NAND_B_1));
  NFET nfet_33 (.G(A_1), .D(A_1_NAND_Carry_0), .S(nfet_33_s));
  NFET nfet_34 (.G(Carry_0), .D(nfet_33_s), .S(GND));
  PFET pfet_34 (.G(Carry_0), .S(Pull_up_Resistor), .D(A_1_NAND_Carry_0));
  PFET pfet_35 (.G(A_5), .S(Pull_up_Resistor), .D(pfet_35_d));
  PFET pfet_36 (.G(A_5_NOT), .S(pfet_35_d), .D(A_5_B_5));
  NFET nfet_35 (.G(A_5), .D(A_5_B_5), .S(nfet_35_s));
  NFET nfet_36 (.G(B_5), .D(nfet_35_s), .S(GND));
  PFET pfet_37 (.G(A_1_NAND_B_1), .S(Pull_up_Resistor), .D(pfet_37_d));
  PFET pfet_38 (.G(A_3), .S(Pull_up_Resistor), .D(pfet_38_d));
  PFET pfet_39 (.G(A_3_NOT), .S(pfet_38_d), .D(A_3_B_3));
  NFET nfet_37 (.G(A_3), .D(A_3_B_3), .S(nfet_37_s));
  NFET nfet_38 (.G(B_3), .D(nfet_37_s), .S(GND));
  PFET pfet_40 (.G(A_7), .S(Pull_up_Resistor), .D(pfet_40_d));
  PFET pfet_41 (.G(A_7_NOT), .S(pfet_40_d), .D(A_7_B_7));
  NFET nfet_39 (.G(A_7), .D(A_7_B_7), .S(nfet_39_s));
  NFET nfet_40 (.G(B_7), .D(nfet_39_s), .S(GND));
  NFET nfet_41 (.G(A_1_NAND_B_1), .D(pfet_37_d), .S(nfet_41_s));
  NFET nfet_42 (.G(A_1_NAND_Carry_0), .D(nfet_41_s), .S(GND));
  PFET pfet_42 (.G(B_5), .S(Pull_up_Resistor), .D(pfet_35_d));
  PFET pfet_43 (.G(B_5_NOT), .S(pfet_35_d), .D(A_5_B_5));
  NFET nfet_43 (.G(A_5_NOT), .D(A_5_B_5), .S(nfet_43_s));
  NFET nfet_44 (.G(B_5_NOT), .D(nfet_43_s), .S(GND));
  PFET pfet_44 (.G(B_3), .S(Pull_up_Resistor), .D(pfet_38_d));
  PFET pfet_45 (.G(B_3_NOT), .S(pfet_38_d), .D(A_3_B_3));
  NFET nfet_45 (.G(A_3_NOT), .D(A_3_B_3), .S(nfet_45_s));
  NFET nfet_46 (.G(B_3_NOT), .D(nfet_45_s), .S(GND));
  PFET pfet_46 (.G(B_7), .S(Pull_up_Resistor), .D(pfet_40_d));
  PFET pfet_47 (.G(B_7_NOT), .S(pfet_40_d), .D(A_7_B_7));
  NFET nfet_47 (.G(A_7_NOT), .D(A_7_B_7), .S(nfet_47_s));
  NFET nfet_48 (.G(B_7_NOT), .D(nfet_47_s), .S(GND));
  PFET pfet_48 (.G(A_1_NAND_Carry_0), .S(Pull_up_Resistor), .D(pfet_37_d));
  PFET pfet_49 (.G(Carry_0), .S(Pull_up_Resistor), .D(B_1_NAND_Carry_0));
  NFET nfet_49 (.G(Carry_0), .D(B_1_NAND_Carry_0), .S(nfet_49_s));
  NFET nfet_50 (.G(B_1), .D(nfet_49_s), .S(GND));
  PFET pfet_50 (.G(A_3_B_3), .S(Pull_up_Resistor), .D(A_3_B_3_NOT));
  NFET nfet_51 (.G(A_3_B_3), .D(A_3_B_3_NOT), .S(GND));
  PFET pfet_51 (.G(A_5_B_5), .S(Pull_up_Resistor), .D(A_5_B_5_NOT));
  NFET nfet_52 (.G(A_5_B_5), .D(A_5_B_5_NOT), .S(GND));
  PFET pfet_52 (.G(A_7_B_7), .S(Pull_up_Resistor), .D(A_7_B_7_NOT));
  NFET nfet_53 (.G(A_7_B_7), .D(A_7_B_7_NOT), .S(GND));
  PFET pfet_53 (.G(pfet_37_d), .S(Pull_up_Resistor), .D(A_1_B_1____Carry_0_A_1));
  NFET nfet_54 (.G(pfet_37_d), .D(A_1_B_1____Carry_0_A_1), .S(GND));
  PFET pfet_54 (.G(B_1), .S(Pull_up_Resistor), .D(B_1_NAND_Carry_0));
  PFET pfet_55 (.G(A_3_B_3), .S(Pull_up_Resistor), .D(pfet_55_d));
  PFET pfet_56 (.G(A_3_B_3_NOT), .S(pfet_55_d), .D(OUT_3));
  NFET nfet_55 (.G(A_3_B_3), .D(OUT_3), .S(nfet_55_s));
  NFET nfet_56 (.G(Carry_2), .D(nfet_55_s), .S(GND));
  PFET pfet_57 (.G(A_5_B_5), .S(Pull_up_Resistor), .D(pfet_57_d));
  PFET pfet_58 (.G(A_5_B_5_NOT), .S(pfet_57_d), .D(OUT_5));
  NFET nfet_57 (.G(A_5_B_5), .D(OUT_5), .S(nfet_57_s));
  NFET nfet_58 (.G(Carry_4), .D(nfet_57_s), .S(GND));
  PFET pfet_59 (.G(A_7_B_7), .S(Pull_up_Resistor), .D(pfet_59_d));
  PFET pfet_60 (.G(A_7_B_7_NOT), .S(pfet_59_d), .D(OUT_7));
  NFET nfet_59 (.G(A_7_B_7), .D(OUT_7), .S(nfet_59_s));
  NFET nfet_60 (.G(Carry_6), .D(nfet_59_s), .S(GND));
  PFET pfet_61 (.G(Carry_2), .S(Pull_up_Resistor), .D(pfet_55_d));
  PFET pfet_62 (.G(C_2_NOT), .S(pfet_55_d), .D(OUT_3));
  NFET nfet_61 (.G(A_3_B_3_NOT), .D(OUT_3), .S(nfet_61_s));
  NFET nfet_62 (.G(C_2_NOT), .D(nfet_61_s), .S(GND));
  PFET pfet_63 (.G(Carry_4), .S(Pull_up_Resistor), .D(pfet_57_d));
  PFET pfet_64 (.G(C_4_NOT), .S(pfet_57_d), .D(OUT_5));
  NFET nfet_63 (.G(A_5_B_5_NOT), .D(OUT_5), .S(nfet_63_s));
  NFET nfet_64 (.G(C_4_NOT), .D(nfet_63_s), .S(GND));
  PFET pfet_65 (.G(Carry_6), .S(Pull_up_Resistor), .D(pfet_59_d));
  PFET pfet_66 (.G(C_6_NOT), .S(pfet_59_d), .D(OUT_7));
  NFET nfet_65 (.G(A_7_B_7_NOT), .D(OUT_7), .S(nfet_65_s));
  NFET nfet_66 (.G(C_6_NOT), .D(nfet_65_s), .S(GND));
  PFET pfet_67 (.G(A_1_B_1____Carry_0_A_1), .S(Pull_up_Resistor), .D(Carry_1));
  NFET nfet_67 (.G(A_1_B_1____Carry_0_A_1), .D(Carry_1), .S(nfet_67_s));
  NFET nfet_68 (.G(B_1_NAND_Carry_0), .D(nfet_67_s), .S(GND));
  PFET pfet_68 (.G(B_1_NAND_Carry_0), .S(Pull_up_Resistor), .D(Carry_1));
  PFET pfet_69 (.G(A_3), .S(Pull_up_Resistor), .D(A_3_NAND_B_3));
  PFET pfet_70 (.G(A_5), .S(Pull_up_Resistor), .D(A_5_NAND_B_5));
  NFET nfet_69 (.G(A_5), .D(A_5_NAND_B_5), .S(nfet_69_s));
  NFET nfet_70 (.G(B_5), .D(nfet_69_s), .S(GND));
  PFET pfet_71 (.G(A_5), .S(Pull_up_Resistor), .D(A_5_NAND_Carry_4));
  PFET pfet_72 (.G(A_7), .S(Pull_up_Resistor), .D(A_7_NAND_B_7));
  PFET pfet_73 (.G(B_3), .S(Pull_up_Resistor), .D(A_3_NAND_B_3));
  NFET nfet_71 (.G(A_3), .D(A_3_NAND_B_3), .S(nfet_71_s));
  NFET nfet_72 (.G(B_3), .D(nfet_71_s), .S(GND));
  PFET pfet_74 (.G(A_3), .S(Pull_up_Resistor), .D(A_3_NAND_Carry_2));
  NFET nfet_73 (.G(A_3), .D(A_3_NAND_Carry_2), .S(nfet_73_s));
  NFET nfet_74 (.G(Carry_2), .D(nfet_73_s), .S(GND));
  PFET pfet_75 (.G(B_5), .S(Pull_up_Resistor), .D(A_5_NAND_B_5));
  NFET nfet_75 (.G(A_5), .D(A_5_NAND_Carry_4), .S(nfet_75_s));
  NFET nfet_76 (.G(Carry_4), .D(nfet_75_s), .S(GND));
  PFET pfet_76 (.G(B_7), .S(Pull_up_Resistor), .D(A_7_NAND_B_7));
  NFET nfet_77 (.G(A_7), .D(A_7_NAND_B_7), .S(nfet_77_s));
  NFET nfet_78 (.G(B_7), .D(nfet_77_s), .S(GND));
  PFET pfet_77 (.G(A_7), .S(Pull_up_Resistor), .D(A_7_NAND_Carry_6));
  NFET nfet_79 (.G(A_7), .D(A_7_NAND_Carry_6), .S(nfet_79_s));
  NFET nfet_80 (.G(Carry_6), .D(nfet_79_s), .S(GND));
  PFET pfet_78 (.G(A_2), .S(Pull_up_Resistor), .D(A_2_NOT));
  NFET nfet_81 (.G(A_2), .D(A_2_NOT), .S(GND));
  PFET pfet_79 (.G(B_2), .S(Pull_up_Resistor), .D(B_2_NOT));
  NFET nfet_82 (.G(B_2), .D(B_2_NOT), .S(GND));
  PFET pfet_80 (.G(Carry_1), .S(Pull_up_Resistor), .D(C_1_NOT));
  NFET nfet_83 (.G(Carry_1), .D(C_1_NOT), .S(GND));
  PFET pfet_81 (.G(Carry_2), .S(Pull_up_Resistor), .D(A_3_NAND_Carry_2));
  PFET pfet_82 (.G(Carry_4), .S(Pull_up_Resistor), .D(A_5_NAND_Carry_4));
  PFET pfet_83 (.G(Carry_6), .S(Pull_up_Resistor), .D(A_7_NAND_Carry_6));
  PFET pfet_84 (.G(A_5_NAND_B_5), .S(Pull_up_Resistor), .D(pfet_84_d));
  PFET pfet_85 (.G(A_3_NAND_B_3), .S(Pull_up_Resistor), .D(pfet_85_d));
  NFET nfet_84 (.G(A_3_NAND_B_3), .D(pfet_85_d), .S(nfet_84_s));
  NFET nfet_85 (.G(A_3_NAND_Carry_2), .D(nfet_84_s), .S(GND));
  NFET nfet_86 (.G(A_5_NAND_B_5), .D(pfet_84_d), .S(nfet_86_s));
  NFET nfet_87 (.G(A_5_NAND_Carry_4), .D(nfet_86_s), .S(GND));
  PFET pfet_86 (.G(A_7_NAND_B_7), .S(Pull_up_Resistor), .D(pfet_86_d));
  NFET nfet_88 (.G(A_7_NAND_B_7), .D(pfet_86_d), .S(nfet_88_s));
  NFET nfet_89 (.G(A_7_NAND_Carry_6), .D(nfet_88_s), .S(GND));
  PFET pfet_87 (.G(A_2), .S(Pull_up_Resistor), .D(pfet_87_d));
  PFET pfet_88 (.G(A_2_NOT), .S(pfet_87_d), .D(A_2_B_2));
  NFET nfet_90 (.G(A_2), .D(A_2_B_2), .S(nfet_90_s));
  NFET nfet_91 (.G(B_2), .D(nfet_90_s), .S(GND));
  PFET pfet_89 (.G(B_2), .S(Pull_up_Resistor), .D(pfet_87_d));
  PFET pfet_90 (.G(B_2_NOT), .S(pfet_87_d), .D(A_2_B_2));
  NFET nfet_92 (.G(A_2_NOT), .D(A_2_B_2), .S(nfet_92_s));
  NFET nfet_93 (.G(B_2_NOT), .D(nfet_92_s), .S(GND));
  PFET pfet_91 (.G(A_3_NAND_Carry_2), .S(Pull_up_Resistor), .D(pfet_85_d));
  PFET pfet_92 (.G(Carry_2), .S(Pull_up_Resistor), .D(B_3_NAND_Carry_2));
  PFET pfet_93 (.G(A_5_NAND_Carry_4), .S(Pull_up_Resistor), .D(pfet_84_d));
  PFET pfet_94 (.G(Carry_4), .S(Pull_up_Resistor), .D(B_5_NAND_Carry_4));
  NFET nfet_94 (.G(Carry_4), .D(B_5_NAND_Carry_4), .S(nfet_94_s));
  NFET nfet_95 (.G(B_5), .D(nfet_94_s), .S(GND));
  PFET pfet_95 (.G(A_7_NAND_Carry_6), .S(Pull_up_Resistor), .D(pfet_86_d));
  PFET pfet_96 (.G(Carry_6), .S(Pull_up_Resistor), .D(B_7_NAND_Carry_6));
  PFET pfet_97 (.G(pfet_85_d), .S(Pull_up_Resistor), .D(A_3_B_3____Carry_2_A_3));
  NFET nfet_96 (.G(pfet_85_d), .D(A_3_B_3____Carry_2_A_3), .S(GND));
  PFET pfet_98 (.G(B_3), .S(Pull_up_Resistor), .D(B_3_NAND_Carry_2));
  NFET nfet_97 (.G(Carry_2), .D(B_3_NAND_Carry_2), .S(nfet_97_s));
  NFET nfet_98 (.G(B_3), .D(nfet_97_s), .S(GND));
  PFET pfet_99 (.G(pfet_84_d), .S(Pull_up_Resistor), .D(A_5_B_5____Carry_4_A_5));
  NFET nfet_99 (.G(pfet_84_d), .D(A_5_B_5____Carry_4_A_5), .S(GND));
  PFET pfet_100 (.G(B_5), .S(Pull_up_Resistor), .D(B_5_NAND_Carry_4));
  PFET pfet_101 (.G(pfet_86_d), .S(Pull_up_Resistor), .D(A_7_B_7____Carry_6_A_7));
  NFET nfet_100 (.G(pfet_86_d), .D(A_7_B_7____Carry_6_A_7), .S(GND));
  PFET pfet_102 (.G(B_7), .S(Pull_up_Resistor), .D(B_7_NAND_Carry_6));
  NFET nfet_101 (.G(Carry_6), .D(B_7_NAND_Carry_6), .S(nfet_101_s));
  NFET nfet_102 (.G(B_7), .D(nfet_101_s), .S(GND));
  PFET pfet_103 (.G(A_2_B_2), .S(Pull_up_Resistor), .D(A_2_B_2_NOT));
  NFET nfet_103 (.G(A_2_B_2), .D(A_2_B_2_NOT), .S(GND));
  PFET pfet_104 (.G(A_2_B_2), .S(Pull_up_Resistor), .D(pfet_104_d));
  PFET pfet_105 (.G(A_2_B_2_NOT), .S(pfet_104_d), .D(OUT_2));
  NFET nfet_104 (.G(A_2_B_2), .D(OUT_2), .S(nfet_104_s));
  NFET nfet_105 (.G(Carry_1), .D(nfet_104_s), .S(GND));
  PFET pfet_106 (.G(A_5_B_5____Carry_4_A_5), .S(Pull_up_Resistor), .D(Carry_5));
  PFET pfet_107 (.G(Carry_1), .S(Pull_up_Resistor), .D(pfet_104_d));
  PFET pfet_108 (.G(C_1_NOT), .S(pfet_104_d), .D(OUT_2));
  NFET nfet_106 (.G(A_2_B_2_NOT), .D(OUT_2), .S(nfet_106_s));
  NFET nfet_107 (.G(C_1_NOT), .D(nfet_106_s), .S(GND));
  PFET pfet_109 (.G(A_3_B_3____Carry_2_A_3), .S(Pull_up_Resistor), .D(Carry_3));
  NFET nfet_108 (.G(A_3_B_3____Carry_2_A_3), .D(Carry_3), .S(nfet_108_s));
  NFET nfet_109 (.G(B_3_NAND_Carry_2), .D(nfet_108_s), .S(GND));
  NFET nfet_110 (.G(A_5_B_5____Carry_4_A_5), .D(Carry_5), .S(nfet_110_s));
  NFET nfet_111 (.G(B_5_NAND_Carry_4), .D(nfet_110_s), .S(GND));
  PFET pfet_110 (.G(A_7_B_7____Carry_6_A_7), .S(Pull_up_Resistor), .D(Carry_out));
  NFET nfet_112 (.G(A_7_B_7____Carry_6_A_7), .D(Carry_out), .S(nfet_112_s));
  NFET nfet_113 (.G(B_7_NAND_Carry_6), .D(nfet_112_s), .S(GND));
  PFET pfet_111 (.G(B_3_NAND_Carry_2), .S(Pull_up_Resistor), .D(Carry_3));
  PFET pfet_112 (.G(B_5_NAND_Carry_4), .S(Pull_up_Resistor), .D(Carry_5));
  PFET pfet_113 (.G(B_7_NAND_Carry_6), .S(Pull_up_Resistor), .D(Carry_out));
  PFET pfet_114 (.G(A_2), .S(Pull_up_Resistor), .D(A_2_NAND_B_2));
  NFET nfet_114 (.G(A_2), .D(A_2_NAND_B_2), .S(nfet_114_s));
  NFET nfet_115 (.G(B_2), .D(nfet_114_s), .S(GND));
  PFET pfet_115 (.G(A_2), .S(Pull_up_Resistor), .D(A_2_NAND_Carry_1));
  PFET pfet_116 (.G(A_4), .S(Pull_up_Resistor), .D(A_4_NOT));
  NFET nfet_116 (.G(A_4), .D(A_4_NOT), .S(GND));
  PFET pfet_117 (.G(B_4), .S(Pull_up_Resistor), .D(B_4_NOT));
  NFET nfet_117 (.G(B_4), .D(B_4_NOT), .S(GND));
  PFET pfet_118 (.G(Carry_3), .S(Pull_up_Resistor), .D(C_3_NOT));
  NFET nfet_118 (.G(Carry_3), .D(C_3_NOT), .S(GND));
  PFET pfet_119 (.G(A_6), .S(Pull_up_Resistor), .D(A_6_NOT));
  NFET nfet_119 (.G(A_6), .D(A_6_NOT), .S(GND));
  PFET pfet_120 (.G(B_6), .S(Pull_up_Resistor), .D(B_6_NOT));
  NFET nfet_120 (.G(B_6), .D(B_6_NOT), .S(GND));
  PFET pfet_121 (.G(Carry_5), .S(Pull_up_Resistor), .D(C_5_NOT));
  NFET nfet_121 (.G(Carry_5), .D(C_5_NOT), .S(GND));
  PFET pfet_122 (.G(B_2), .S(Pull_up_Resistor), .D(A_2_NAND_B_2));
  NFET nfet_122 (.G(A_2), .D(A_2_NAND_Carry_1), .S(nfet_122_s));
  NFET nfet_123 (.G(Carry_1), .D(nfet_122_s), .S(GND));
  PFET pfet_123 (.G(Carry_1), .S(Pull_up_Resistor), .D(A_2_NAND_Carry_1));
  PFET pfet_124 (.G(A_4), .S(Pull_up_Resistor), .D(pfet_124_d));
  PFET pfet_125 (.G(A_4_NOT), .S(pfet_124_d), .D(A_4_B_4));
  NFET nfet_124 (.G(A_4), .D(A_4_B_4), .S(nfet_124_s));
  NFET nfet_125 (.G(B_4), .D(nfet_124_s), .S(GND));
  PFET pfet_126 (.G(A_6), .S(Pull_up_Resistor), .D(pfet_126_d));
  PFET pfet_127 (.G(A_6_NOT), .S(pfet_126_d), .D(A_6_B_6));
  NFET nfet_126 (.G(A_6), .D(A_6_B_6), .S(nfet_126_s));
  NFET nfet_127 (.G(B_6), .D(nfet_126_s), .S(GND));
  PFET pfet_128 (.G(A_2_NAND_B_2), .S(Pull_up_Resistor), .D(pfet_128_d));
  NFET nfet_128 (.G(A_2_NAND_B_2), .D(pfet_128_d), .S(nfet_128_s));
  NFET nfet_129 (.G(A_2_NAND_Carry_1), .D(nfet_128_s), .S(GND));
  PFET pfet_129 (.G(B_4), .S(Pull_up_Resistor), .D(pfet_124_d));
  PFET pfet_130 (.G(B_4_NOT), .S(pfet_124_d), .D(A_4_B_4));
  NFET nfet_130 (.G(A_4_NOT), .D(A_4_B_4), .S(nfet_130_s));
  NFET nfet_131 (.G(B_4_NOT), .D(nfet_130_s), .S(GND));
  PFET pfet_131 (.G(B_6), .S(Pull_up_Resistor), .D(pfet_126_d));
  PFET pfet_132 (.G(B_6_NOT), .S(pfet_126_d), .D(A_6_B_6));
  NFET nfet_132 (.G(A_6_NOT), .D(A_6_B_6), .S(nfet_132_s));
  NFET nfet_133 (.G(B_6_NOT), .D(nfet_132_s), .S(GND));
  PFET pfet_133 (.G(A_2_NAND_Carry_1), .S(Pull_up_Resistor), .D(pfet_128_d));
  PFET pfet_134 (.G(Carry_1), .S(Pull_up_Resistor), .D(B_2_NAND_Carry_1));
  PFET pfet_135 (.G(pfet_128_d), .S(Pull_up_Resistor), .D(A_2_B_2____Carry_1_A_2));
  NFET nfet_134 (.G(pfet_128_d), .D(A_2_B_2____Carry_1_A_2), .S(GND));
  PFET pfet_136 (.G(B_2), .S(Pull_up_Resistor), .D(B_2_NAND_Carry_1));
  NFET nfet_135 (.G(Carry_1), .D(B_2_NAND_Carry_1), .S(nfet_135_s));
  NFET nfet_136 (.G(B_2), .D(nfet_135_s), .S(GND));
  PFET pfet_137 (.G(A_4_B_4), .S(Pull_up_Resistor), .D(A_4_B_4_NOT));
  NFET nfet_137 (.G(A_4_B_4), .D(A_4_B_4_NOT), .S(GND));
  PFET pfet_138 (.G(A_6_B_6), .S(Pull_up_Resistor), .D(A_6_B_6_NOT));
  NFET nfet_138 (.G(A_6_B_6), .D(A_6_B_6_NOT), .S(GND));
  PFET pfet_139 (.G(A_4_B_4), .S(Pull_up_Resistor), .D(pfet_139_d));
  PFET pfet_140 (.G(A_4_B_4_NOT), .S(pfet_139_d), .D(OUT_4));
  NFET nfet_139 (.G(A_4_B_4), .D(OUT_4), .S(nfet_139_s));
  NFET nfet_140 (.G(Carry_3), .D(nfet_139_s), .S(GND));
  PFET pfet_141 (.G(A_6_B_6), .S(Pull_up_Resistor), .D(pfet_141_d));
  PFET pfet_142 (.G(A_6_B_6_NOT), .S(pfet_141_d), .D(OUT_6));
  NFET nfet_141 (.G(A_6_B_6), .D(OUT_6), .S(nfet_141_s));
  NFET nfet_142 (.G(Carry_5), .D(nfet_141_s), .S(GND));
  PFET pfet_143 (.G(Carry_5), .S(Pull_up_Resistor), .D(pfet_141_d));
  PFET pfet_144 (.G(C_5_NOT), .S(pfet_141_d), .D(OUT_6));
  PFET pfet_145 (.G(Carry_3), .S(Pull_up_Resistor), .D(pfet_139_d));
  PFET pfet_146 (.G(C_3_NOT), .S(pfet_139_d), .D(OUT_4));
  NFET nfet_143 (.G(A_4_B_4_NOT), .D(OUT_4), .S(nfet_143_s));
  NFET nfet_144 (.G(C_3_NOT), .D(nfet_143_s), .S(GND));
  NFET nfet_145 (.G(A_6_B_6_NOT), .D(OUT_6), .S(nfet_145_s));
  NFET nfet_146 (.G(C_5_NOT), .D(nfet_145_s), .S(GND));
  PFET pfet_147 (.G(A_2_B_2____Carry_1_A_2), .S(Pull_up_Resistor), .D(Carry_2));
  NFET nfet_147 (.G(A_2_B_2____Carry_1_A_2), .D(Carry_2), .S(nfet_147_s));
  NFET nfet_148 (.G(B_2_NAND_Carry_1), .D(nfet_147_s), .S(GND));
  PFET pfet_148 (.G(B_2_NAND_Carry_1), .S(Pull_up_Resistor), .D(Carry_2));
  PFET pfet_149 (.G(A_6), .S(Pull_up_Resistor), .D(A_6_NAND_B_6));
  PFET pfet_150 (.G(A_4), .S(Pull_up_Resistor), .D(A_4_NAND_B_4));
  NFET nfet_149 (.G(A_4), .D(A_4_NAND_B_4), .S(nfet_149_s));
  NFET nfet_150 (.G(B_4), .D(nfet_149_s), .S(GND));
  PFET pfet_151 (.G(A_4), .S(Pull_up_Resistor), .D(A_4_NAND_Carry_3));
  PFET pfet_152 (.G(B_6), .S(Pull_up_Resistor), .D(A_6_NAND_B_6));
  NFET nfet_151 (.G(A_6), .D(A_6_NAND_B_6), .S(nfet_151_s));
  NFET nfet_152 (.G(B_6), .D(nfet_151_s), .S(GND));
  PFET pfet_153 (.G(A_6), .S(Pull_up_Resistor), .D(A_6_NAND_Carry_5));
  NFET nfet_153 (.G(A_6), .D(A_6_NAND_Carry_5), .S(nfet_153_s));
  NFET nfet_154 (.G(Carry_5), .D(nfet_153_s), .S(GND));
  PFET pfet_154 (.G(B_4), .S(Pull_up_Resistor), .D(A_4_NAND_B_4));
  NFET nfet_155 (.G(A_4), .D(A_4_NAND_Carry_3), .S(nfet_155_s));
  NFET nfet_156 (.G(Carry_3), .D(nfet_155_s), .S(GND));
  PFET pfet_155 (.G(Carry_5), .S(Pull_up_Resistor), .D(A_6_NAND_Carry_5));
  PFET pfet_156 (.G(Carry_3), .S(Pull_up_Resistor), .D(A_4_NAND_Carry_3));
  PFET pfet_157 (.G(A_4_NAND_B_4), .S(Pull_up_Resistor), .D(pfet_157_d));
  PFET pfet_158 (.G(A_6_NAND_B_6), .S(Pull_up_Resistor), .D(pfet_158_d));
  NFET nfet_157 (.G(A_4_NAND_B_4), .D(pfet_157_d), .S(nfet_157_s));
  NFET nfet_158 (.G(A_4_NAND_Carry_3), .D(nfet_157_s), .S(GND));
  NFET nfet_159 (.G(A_6_NAND_B_6), .D(pfet_158_d), .S(nfet_159_s));
  NFET nfet_160 (.G(A_6_NAND_Carry_5), .D(nfet_159_s), .S(GND));
  PFET pfet_159 (.G(A_4_NAND_Carry_3), .S(Pull_up_Resistor), .D(pfet_157_d));
  PFET pfet_160 (.G(Carry_3), .S(Pull_up_Resistor), .D(B_4_NAND_Carry_3));
  NFET nfet_161 (.G(Carry_3), .D(B_4_NAND_Carry_3), .S(nfet_161_s));
  NFET nfet_162 (.G(B_4), .D(nfet_161_s), .S(GND));
  PFET pfet_161 (.G(A_6_NAND_Carry_5), .S(Pull_up_Resistor), .D(pfet_158_d));
  PFET pfet_162 (.G(pfet_158_d), .S(Pull_up_Resistor), .D(A_6_B_6____Carry_5_A_6));
  NFET nfet_163 (.G(pfet_158_d), .D(A_6_B_6____Carry_5_A_6), .S(GND));
  PFET pfet_163 (.G(Carry_5), .S(Pull_up_Resistor), .D(B_6_NAND_Carry_5));
  NFET nfet_164 (.G(Carry_5), .D(B_6_NAND_Carry_5), .S(nfet_164_s));
  NFET nfet_165 (.G(B_6), .D(nfet_164_s), .S(GND));
  PFET pfet_164 (.G(pfet_157_d), .S(Pull_up_Resistor), .D(A_4_B_4____Carry_3_A_4));
  NFET nfet_166 (.G(pfet_157_d), .D(A_4_B_4____Carry_3_A_4), .S(GND));
  PFET pfet_165 (.G(B_4), .S(Pull_up_Resistor), .D(B_4_NAND_Carry_3));
  PFET pfet_166 (.G(B_6), .S(Pull_up_Resistor), .D(B_6_NAND_Carry_5));
  PFET pfet_167 (.G(A_4_B_4____Carry_3_A_4), .S(Pull_up_Resistor), .D(Carry_4));
  PFET pfet_168 (.G(A_6_B_6____Carry_5_A_6), .S(Pull_up_Resistor), .D(Carry_6));
  NFET nfet_167 (.G(A_4_B_4____Carry_3_A_4), .D(Carry_4), .S(nfet_167_s));
  NFET nfet_168 (.G(B_4_NAND_Carry_3), .D(nfet_167_s), .S(GND));
  NFET nfet_169 (.G(A_6_B_6____Carry_5_A_6), .D(Carry_6), .S(nfet_169_s));
  NFET nfet_170 (.G(B_6_NAND_Carry_5), .D(nfet_169_s), .S(GND));
  PFET pfet_169 (.G(B_4_NAND_Carry_3), .S(Pull_up_Resistor), .D(Carry_4));
  PFET pfet_170 (.G(B_6_NAND_Carry_5), .S(Pull_up_Resistor), .D(Carry_6));

  // Notes on the sheet:
  //   Value A
  //   Value B
  //   Result (A + B)
  //   NOT gate
  //   A_0 + B_0
  //   XOR Gate
  //   3 - input XOR Gate (A_1 + B_1)
  //   Carry for A_0 + B_0
  //   AND Gate
  //   3 - input XOR Gate (A_5 + B_5)
  //   Carry for A_1 + B_1 ((Carry & A) || (Carry & B) || (A & B))
  //   3 - input XOR Gate (A_3 + B_3)
  //   3 - input XOR Gate (A_7 + B_7)
  //   Carry for A_3 + B_3 ((Carry & A) || (Carry & B) || (A & B))
  //   Carry for A_5+ B_5 ((Carry & A) || (Carry & B) || (A & B))
  //   Carry for A_7+ B_7 ((Carry & A) || (Carry & B) || (A & B))
  //   3 - input XOR Gate (A_2 + B_2)
  //   Carry for A_2 + B_2 ((Carry & A) || (Carry & B) || (A & B))
  //   3 - input XOR Gate (A_4 + B_4)
  //   3 - input XOR Gate (A_6 + B_6)
  //   Carry for A_4 + B_4 ((Carry & A) || (Carry & B) || (A & B))
  //   Carry for A_6+ B_6 ((Carry & A) || (Carry & B) || (A & B))
endmodule
